# Fritzing sketch Lydhorn (saved by Fritzing 0.9.3b)
breadboards: 1

parts:
  SPKR1 = Loudspeaker
  Part1 = Arduino Uno (Rev3)
  Q1 = NPN-Transistor [package="TO92 [THT]"]
  R1 = Resistor [tolerance=±5% resistance=220 package=THT]

nets:
  N1: SPKR1.pin1, Q1.E
  N2: SPKR1.pin2, Part1.5V
  N3: Part1.GND, Q1.C
  N4: Part1.D2, R1.Pin_1
  N5: Q1.B, R1.Pin_0
